# Fritzing sketch Systéme final (saved by Fritzing 0.9.3b)

parts:
  Composant5 = Arduino Pro Mini v13
  LED1 = smd LED [color="Red (633nm)" package="1206 [SMD]"]
  R1 = Resistor [tolerance=±5% resistance=220 package="0603 [SMD]"]
  TRS1 = Audio Jack (TRS) 3.5mm [package="PG203J [THT]"]
  J1 = Basic Servo
  U4 = Voltage Regulator [package=to220-adj]
  BAT1 = BC9VPC [package=bc9vpc]
  20uF = Capacitor Polarized [package=panasonic_c]
  C1 = Capacitor [package=cap-pth-small2]
  U5 = Voltage Regulator [package=to220-adj]
  BAT2 = BC9VPC [package=bc9vpc]
  20uF1 = Capacitor Polarized [package=panasonic_c]
  C2 = Capacitor [package=cap-pth-small2]
  S3 = Toggle Switch [package=THT]
  S4 = Toggle Switch [package=THT]
  LED2 = smd LED [color="Green (555nm)" package="1206 [SMD]"]
  R19 = Resistor [tolerance=±5% resistance=220 package="0603 [SMD]"]
  U6 = TLP621 [package=THT]
  U7 = TLP621 [package=THT]
  Mod1 = ossoyoo-lora-module
  R20 = Resistor [tolerance=±5% resistance=470 package="0805 [SMD]"]
  R23 = Resistor [tolerance=±5% resistance=2.2k package="0805 [SMD]"]
  R24 = Resistor [tolerance=±5% resistance=1k package="0805 [SMD]"]
  Composant3 = Arduino Pro Mini v13
  R25 = Resistor [tolerance=±5% resistance=220 package="0805 [SMD]"]
  R26 = Resistor [tolerance=±5% resistance=220 package="0805 [SMD]"]
  R27 = Resistor [tolerance=±5% resistance=220 package="0805 [SMD]"]
  R28 = Resistor [tolerance=±5% resistance=220 package="0805 [SMD]"]
  Composant6 = InvenSense MPU6050
  M1 = BME280
  Composant7 = MicroSD Card Module

nets:
  N1: Composant5.D1/RX, U6.Pin_4, R28.Pin_0
  N2: Composant5.RAW, U4.ADJ, 20uF.-, S3.L2, R25.Pin_1, R28.Pin_1
  N3: Composant5.GND, U6.Pin_3
  N4: Composant5.D11_PWM/MOSI, J1.pulse
  N5: Composant5.D10_PWM/SS, LED2.cathode
  N6: Composant5.D9_PWM, TRS1.Tip
  N7: Composant5.D0/TX, U7.Pin_2
  N8: LED1.cathode, Composant3.D8
  N9: LED1.anode, R1.Pin_0
  GND: R1.Pin_1, BAT2.V-, U7.Pin_3, Mod1.M0, Mod1.M1, Mod1.GND, R23.Pin_1, Composant3.GND, M1.GND
  N10: J1.gnd, BAT1.V-, R19.Pin_1
  N11: J1.vcc, U4.OUT, C1.1
  N12: U4.IN, 20uF.+, C1.2
  N13: BAT1.V+, S3.COM
  N14: U5.ADJ, 20uF1.-, S4.L2, Composant3.RAW, R26.Pin_1, R27.Pin_0
  N15: U5.IN, 20uF1.+, C2.2
  VCC: U5.OUT, C2.1, Mod1.VCC, Composant6.VCC
  N16: BAT2.V+, S4.COM
  N17: U6.Pin_1, R27.Pin_1
  N18: U6.Pin_2, Composant3.D0/TX
  N19: U7.Pin_1, R25.Pin_0
  N20: U7.Pin_4, Composant3.D1/RX, R26.Pin_0
  N21: Mod1.RXD, R20.Pin_0, R23.Pin_0, R24.Pin_0
  VCC_2: R20.Pin_1, Composant3.VCC, M1.VIN, Composant7.VCC
  N22: R24.Pin_1, Composant3.D7
  N23: Composant3.A4, Composant6.SDA, M1.SDA
  N24: Composant3.A5, Composant6.SCL, M1.SCL
  N25: Composant3.D13/SCK, Composant7.SCK
  N26: Composant3.D12/MISO, Composant7.MISO
  N27: Composant3.D11_PWM/MOSI, Composant7.MOSI
  N28: Composant3.D10_PWM/SS, Composant7.CS
  GND_2: Composant6.GND, Composant7.GND

notes:
  5v
  22 uF
  0.01 uF
  L7805
  470 ohms
  1K ohms
  2K ohms
  220 ohms
  9V
  330 Ohms
  2K Ohms

custom parts:
  ossoyoo-lora-module: Osoyoo Long Distance wireless transceiver Uart LoRa Module.
  BME280: Temperature Humidity Barometric presure Sensor
