# Fritzing sketch Untitled Sketch (saved by Fritzing 0.9.3b)
perfboards: 1

parts:
  Composant1 = Arduino Uno (Rev3)  # not connected
  Mod2 = ossoyoo-lora-module
  R1 = Resistor [tolerance=±5% resistance=330 package="0603 [SMD]"]
  R2 = Resistor [tolerance=±5% resistance=330 package="0603 [SMD]"]
  R3 = Resistor [tolerance=±5% resistance=1k package="0603 [SMD]"]
  R4 = Resistor [tolerance=±5% resistance=2k package="0603 [SMD]"]

nets:
  N1: Mod2.M0, Mod2.M1, Mod2.GND, R4.Pin_1
  N2: Mod2.RXD, R1.Pin_0
  N3: Mod2.TXD, R2.Pin_0, R3.Pin_1, R4.Pin_0
  N4: R1.Pin_1, R2.Pin_1

custom parts:
  ossoyoo-lora-module: Osoyoo Long Distance wireless transceiver Uart LoRa Module.
