# Fritzing sketch enregistreur de vol (saved by Fritzing 0.9.3b)

parts:
  Composant3 = Arduino Pro Mini v13
  Composant5 = Arduino Pro Mini v13
  LED1 = smd LED [color="Red (633nm)" package="1206 [SMD]"]
  R1 = Resistor [tolerance=±5% resistance=220 package="0603 [SMD]"]  # not connected
  TRS1 = Audio Jack (TRS) 3.5mm [package="PG203J [THT]"]
  J1 = Basic Servo
  U1 = TLP621 [package=THT]
  U2 = TLP621 [package=THT]
  U3 = TLP621 [package=THT]
  R5 = Resistor [tolerance=±5% resistance=220 package=THT]
  R6 = Resistor [tolerance=±5% resistance=220 package=THT]
  R7 = Resistor [tolerance=±5% resistance=220 package=THT]
  U4 = Voltage Regulator [package=to220-adj]
  BAT1 = BC9VPC [package=bc9vpc]
  20uF = Capacitor Polarized [package=panasonic_c]
  C1 = Capacitor [package=cap-pth-small2]
  U5 = Voltage Regulator [package=to220-adj]
  BAT2 = BC9VPC [package=bc9vpc]
  20uF1 = Capacitor Polarized [package=panasonic_c]
  C2 = Capacitor [package=cap-pth-small2]
  S3 = Toggle Switch [package=THT]
  S4 = Toggle Switch [package=THT]
  Composant7 = MicroSD Card Module
  M2 = BMP280
  Composant8 = InvenSense MPU6050
  R18 = Resistor [tolerance=±5% resistance=220 package="2512 [SMD]"]
  LED2 = smd LED [color="Green (555nm)" package="1206 [SMD]"]
  R19 = Resistor [tolerance=±5% resistance=220 package="0603 [SMD]"]
  R10 = Resistor [tolerance=±5% resistance=220 package=THT]
  R20 = Resistor [tolerance=±5% resistance=220 package=THT]
  R21 = Resistor [tolerance=±5% resistance=220 package=THT]

nets:
  VCC: Composant3.VCC, Composant7.VCC, R21.Pin_0
  N1: Composant3.GND, U2.Pin_2, U3.Pin_3, BAT2.V-
  N2: Composant3.RAW, U5.ADJ, 20uF1.-, S4.L2
  N3: Composant3.A1, U3.Pin_4, R21.Pin_1
  N4: Composant3.A0, U1.Pin_4, R10.Pin_1
  N5: Composant3.D8, LED1.cathode
  N6: Composant3.D5_PWM, R7.Pin_0
  N7: Composant3.D2, Composant8.INT
  N8: Composant5.RAW, U4.ADJ, 20uF.-, S3.L2
  N9: Composant5.VCC, R18.Pin_0, R20.Pin_1
  N10: Composant5.D11_PWM/MOSI, J1.pulse
  N11: Composant5.D9_PWM, TRS1.Tip, R18.Pin_1
  N12: Composant5.D8, R6.Pin_0
  N13: Composant5.D7, R5.Pin_0
  N14: Composant5.D6_PWM, LED2.cathode
  N15: Composant5.D5_PWM, U2.Pin_4, R20.Pin_0
  N16: J1.gnd, U3.Pin_2, BAT1.V-, R19.Pin_1
  N17: J1.vcc, U4.OUT, C1.1
  N18: U4.IN, 20uF.+, C1.2
  N19: BAT1.V+, S3.COM
  N20: U5.IN, 20uF1.+, C2.2
  N21: U5.OUT, C2.1
  N22: BAT2.V+, S4.COM
  N23: M2.VIN, R10.Pin_0

notes:
  Com1
  OrdreOuverture
  Com2
  5v
  220 Hom
  22 uF
  0.01 uF
  L7805
  3.3v

custom parts:
  MicroSD Card Module: A common microSD card module.
  BMP280: Temperature Humidity Barometric presure Sensor, I2C
