# Fritzing sketch test (saved by Fritzing 0.9.3b)

parts:
  Composant1 = Arduino Uno (Rev3)
  GY2 = MPU-6050 Board GY-521 [form="♀ (female)" package=THT]
  M1 = BME280
  Composant3 = Arduino Pro Mini v13
  Composant4 = MicroSD Card Module

nets (from the breadboard view):
  GND: Composant1.GND, GY2.pin2, M1.GND, Composant3.GND, Composant4.GND
  N1: Composant1.D0/RX, Composant3.D1/RX
  N2: Composant1.D1/TX, Composant3.D0/TX
  N3: Composant1.RESET, Composant3.DTR
  VCC: Composant1.3V3, M1.VIN, Composant3.VCC, Composant4.VCC
  N4: Composant1.5V, GY2.pin1
  N5: GY2.pin3, M1.SCL, Composant3.A5
  N6: GY2.pin4, M1.SDA, Composant3.A4
  N7: GY2.pin8, Composant3.D2
  N8: Composant3.D13/SCK, Composant4.SCK
  N9: Composant3.D12/MISO, Composant4.MISO
  N10: Composant3.D11_PWM/MOSI, Composant4.MOSI
  N11: Composant3.D4, Composant4.CS

custom parts:
  MPU-6050 Board GY-521: Acelerometro y Giroscopio MPU-6050 Board GY-521
  BME280: Temperature Humidity Barometric presure Sensor
  MicroSD Card Module: A common microSD card module.
