# Fritzing sketch PCB (saved by Fritzing 0.9.3b)
circuit board: 10cm x 5cm
breadboards: 1

parts:
  Régulateur_de_tension_Seq = Voltage Regulator [package=to220-adj]
  BAT3 = BC9VPC [package=bc9vpc]  # not connected
  BAT4 = BC9VPC [package=bc9vpc]  # not connected
  Servo = Basic Servo
  Octocoupleur_Exp = TLP621 [package=THT]
  Carte_Exp = Arduino Pro Mini v13
  Carte_Séquenceur = Arduino Pro Mini v13
  Octocoupleur_Seq = TLP621 [package=THT]
  Régulateur_de_tension_Exp = Voltage Regulator [package=to220-adj]

nets:
  N1: Régulateur_de_tension_Seq.ADJ, Carte_Séquenceur.RAW
  N2: Régulateur_de_tension_Seq.IN, Servo.vcc
  GND: Régulateur_de_tension_Seq.OUT, Servo.gnd, Octocoupleur_Exp.Pin_3, Carte_Séquenceur.GND
  N3: Servo.pulse, Carte_Séquenceur.D11_PWM/MOSI
  N4: Octocoupleur_Exp.Pin_2, Carte_Exp.D0/TX
  N5: Octocoupleur_Exp.Pin_4, Carte_Séquenceur.D1/RX
  N6: Carte_Exp.D1/RX, Octocoupleur_Seq.Pin_4
  N7: Carte_Exp.RAW, Régulateur_de_tension_Exp.ADJ
  N8: Carte_Exp.GND, Octocoupleur_Seq.Pin_3, Régulateur_de_tension_Exp.OUT
  N9: Carte_Séquenceur.D6_PWM, Carte_Séquenceur.D5_PWM
  N10: Carte_Séquenceur.D0/TX, Octocoupleur_Seq.Pin_2

notes:
  jack
  led Seq
  2K
  330
  5v
  3.3v
  GND
  cs
  MOSI
  MISO
  SCK
  C DET
  SCL
  SDA
  220
  470
  1K
  led Exp
